# Fritzing sketch Agrina Module (saved by Fritzing 0.9.5d)

parts:
  A1 = LoRa sx1278 module [package=THT]
  Part1 = Arduino Nano (Rev3.0)
  M1 = PH meter with sensor in breadboard [package=THT]
  A2 = JXBS-3001-NPK-RS
  DS1 = DS18B20 1-Wire Temperature Sensor Probe
  Part2 = Adafruit BQ24074 Solar-DC-USB Lipo Charger
  JACK1 = 2.1mm Barrel Jack with Terminal Block  # not connected
  U2 = LIPO-1000mAh [package=lipo-1000]

nets:
  GND: A1.Pin_1, A1.Pin_12, A1.Pin_15, Part1.GND, M1.pin3, A2.Pin_2, DS1.GND, Part2.GND, U2.-
  5V: A1.Pin_5, Part1.5V, M1.pin2, A2.Pin_1, DS1.VDD, Part2.OUT
  N1: A1.Pin_6, Part1.D12/MISO
  N2: A1.Pin_7, Part1.D11/MOSI
  N3: A1.Pin_8, Part1.D13/SCK
  N4: A1.Pin_9, Part1.D10
  N5: A1.Pin_10, Part1.D2
  N6: A1.Pin_11, Part1.D9
  N7: Part1.D3, A2.Pin_3
  N8: Part1.D4, A2.Pin_4
  N9: Part1.D5, DS1.DQ
  N10: Part1.A0, M1.pin1
  N11: Part2.VLIPO, U2.+

custom parts:
  LoRa sx1278 module: SX1278 Long Range RF Wireless Power Mental Module.
  PH meter with sensor in breadboard: DFrobot PH meter (SKU SEN0161)
  JXBS-3001-NPK-RS: The NPK sensor is designed for detecting the content of nitrogen, phosphorus and potassium in soil, determining the fertility of the soil and facilitating the evaluation of the soil condition by the customer system.
