# Fritzing sketch Agrina Receiver Module (saved by Fritzing 0.9.5d)

parts:
  esp1 = ESP32 DevKitc V4
  A1 = LoRa sx1278 module [package=THT]

nets:
  N1: esp1.IO4, A1.Pin_11
  N2: esp1.IO16, A1.Pin_10
  N3: esp1.IO17, A1.Pin_9
  N4: esp1.IO18, A1.Pin_8
  N5: esp1.IO19, A1.Pin_6
  N6: esp1.IO23, A1.Pin_7
  N7: esp1.GND, A1.Pin_12, A1.Pin_15
  N8: esp1.5V, A1.Pin_5

custom parts:
  ESP32 DevKitc V4: ESP32-DevKitC board with ESP32-WROOM-32 module. ESP32-DevKitC V4 is a small-sized ESP32-based development board produced by Espressif. Most of the pins on the ESP module are broken out to the pin headers on the board. The pins D0, D1, D2, D3, CMD and CLK are used internally for communication between ESP32 and SPI flash memory. They are grouped on both sides near the USB connector. Avoid using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
  LoRa sx1278 module: SX1278 Long Range RF Wireless Power Mental Module.
